# Fritzing sketch D_7_2_i_2_light_source (saved by Fritzing 0.9.2b)
breadboards: 2

parts:
  パーツ1 = Arduino Uno (Rev3) - ICSP
  U1 = LCD-16X2 [package=lcd-16x2_noholes]  # not connected
  R1 = PHOTOCELL [package=photocell-kit]
  R2 = Resistor [tolerance=±5% resistance=220 package="0805 [SMD]"]
  R3 = PHOTOCELL [package=photocell-kit]
  R4 = Resistor [tolerance=±5% resistance=220 package="0805 [SMD]"]
  R5 = PHOTOCELL [package=photocell-kit]
  R6 = Resistor [tolerance=±5% resistance=220 package="0805 [SMD]"]
  R7 = Resistor [tolerance=±5% resistance=220 package="0805 [SMD]"]
  LED1 = smd LED [color="Red (633nm)" package="0805 [SMD]"]
  R8 = Resistor [tolerance=±5% resistance=220 package="0805 [SMD]"]
  LED2 = smd LED [color="Red (633nm)" package="0805 [SMD]"]
  R9 = Resistor [tolerance=±5% resistance=220 package="0805 [SMD]"]
  LED3 = smd LED [color="Red (633nm)" package="0805 [SMD]"]
  R10 = Resistor [tolerance=±5% resistance=220 package="0805 [SMD]"]
  LED4 = smd LED [color="Red (633nm)" package="0805 [SMD]"]
  R11 = Resistor [tolerance=±5% resistance=220 package="0805 [SMD]"]
  LED5 = smd LED [color="Red (633nm)" package="0805 [SMD]"]

nets:
  N1: パーツ1.A0, R5.P$1, R6.Pin_1
  N2: パーツ1.A1, R3.P$1, R4.Pin_1
  N3: パーツ1.A2, R1.P$1, R2.Pin_1
  N4: パーツ1.5V, R1.P$2, R3.P$2, R5.P$2
  N5: パーツ1.GND, R2.Pin_0, R4.Pin_0, R6.Pin_0, LED1.cathode, LED2.cathode, LED3.cathode, LED4.cathode, LED5.cathode
  N6: パーツ1.D2, R7.Pin_0
  N7: パーツ1.D3_PWM, R8.Pin_0
  N8: パーツ1.D4, R9.Pin_0
  N9: パーツ1.D5_PWM, R10.Pin_0
  N10: パーツ1.D6_PWM, R11.Pin_0
  N11: R7.Pin_1, LED1.anode
  N12: R8.Pin_1, LED2.anode
  N13: R9.Pin_1, LED3.anode
  N14: R10.Pin_1, LED4.anode
  N15: R11.Pin_1, LED5.anode
